// Logisim project ALU.circ as structural Verilog: 2 circuits, main circuit ALU
module ALU (
  input  [31:0] rs1,
  input  [31:0] rs2_imm,
  input  [3:0] opSel,
  output [31:0] rd
);

  wire comparator_1_lt, comparator_2_lt;
  wire [31:0] adder_1_out, and_1_out, bit_extender_1_out, bit_extender_2_out, or_1_out, shifter_1_out,
       shifter_2_out, shifter_3_out, subtractor_1_out, xor_1_out;

  assign or_1_out = rs1 | rs2_imm;  // OR_Gate or_1, 32 bits wide
  assign and_1_out = rs1 & rs2_imm;  // AND_Gate and_1, 32 bits wide
  Adder #(.width(32)) adder_1 (.a(rs1), .b(rs2_imm), .out(adder_1_out));  // open: cin, cout
  Shifter #(.width(32)) shifter_1 (.in(rs1), .\dist (rs2_imm[4:0]), .out(shifter_1_out));
  Comparator #(.width(32)) comparator_1 (.a(rs1), .b(rs2_imm), .lt(comparator_1_lt));  // open: gt, eq
  assign bit_extender_1_out = {{31{1'b0}}, comparator_1_lt};  // Bit_Extender bit_extender_1
  Comparator #(.width(32), .mode("unsigned")) comparator_2 (
    .a(rs1), .b(rs2_imm), .lt(comparator_2_lt));  // open: gt, eq
  assign bit_extender_2_out = {{31{1'b0}}, comparator_2_lt};  // Bit_Extender bit_extender_2
  assign xor_1_out = rs1 ^ rs2_imm;  // XOR_Gate xor_1, 32 bits wide
  Shifter #(.width(32), .shift("lr")) shifter_2 (.in(rs1), .\dist (rs2_imm[4:0]), .out(shifter_2_out));
  Subtractor #(.width(32)) subtractor_1 (.a(rs1), .b(rs2_imm), .out(subtractor_1_out));  // open: bin, bout
  Shifter #(.width(32), .shift("ar")) shifter_3 (.in(rs1), .\dist (rs2_imm[4:0]), .out(shifter_3_out));
  Multiplexer #(.select(4), .width(32), .enable("false")) multiplexer_1 (
    .in0(adder_1_out), .in1(shifter_1_out), .in2(bit_extender_1_out), .in3(bit_extender_2_out),
    .in4(xor_1_out), .in5(shifter_2_out), .in6(or_1_out), .in7(and_1_out), .in8(subtractor_1_out),
    .in13(shifter_3_out), .out(rd), .sel(opSel));  // open: in9, in10, in11, in12, in14, in15
endmodule

module Test (
  input  [31:0] rs1_Data,
  input  [31:0] rs2_Data,
  input  [3:0] opSelecter,
  output [31:0] rd_Data
);

  ALU alu_1 (.rs1(rs1_Data), .rs2_imm(rs2_Data), .opSel(opSelecter), .rd(rd_Data));
endmodule
