// Logisim project Controller.circ as structural Verilog: 1 circuit, main circuit main
module main (
  input  [4:0] opcIn,
  output Load_En,
  output Save_En
);

  wire comparator_1_lt;
  wire [1:0] undriven;
  wire [2:0] bit_extender_1_out, bitselector_1_out;

  Comparator #(.width(2)) comparator_1 (.a(2'b11), .b(opcIn[1:0]), .lt(comparator_1_lt));  // open: gt, eq
  Bit_Extender #(.in_width(5), .out_width(3)) bit_extender_1 (
    .in({undriven, opcIn[2], opcIn[4:3]}), .out(bit_extender_1_out));
  Decoder #(.select(3), .enable("false")) decoder_1 (
    .out0(Load_En), .out1(Save_En), .sel(bitselector_1_out));  // open: out2, out3, out4, out5, out6, out7
  BitSelector #(.width(3), .group(3)) bitselector_1 (
    .in(bit_extender_1_out), .out(bitselector_1_out), .sel(comparator_1_lt));
endmodule
