// Logisim project Decoder.circ as structural Verilog: 9 circuits, main circuit Decoder
module Decoder (
  input  [31:0] Data,
  output [6:0] opcode,
  output [4:0] rd,
  output [2:0] func3,
  output [4:0] rs1,
  output [4:0] rs2,
  output [6:0] func7,
  output [31:0] imm
);

  wire decoder_1_out0, decoder_1_out3, decoder_1_out4, decoder_1_out5, decoder_1_out6, decoder_1_out8,
       decoder_1_out12, decoder_1_out13, decoder_1_out14, decoder_1_out24, decoder_1_out25, decoder_1_out27,
       decoder_1_out28, or_1_out, or_2_out, or_3_out, or_4_out, or_5_out, or_6_out, or_7_out, or_8_out;
  wire [2:0] i_1_func3, r_1_func3, s_1_func3, sb_1_func3;
  wire [3:0] bit_extender_1_out;
  wire [4:0] i_1_rd, i_1_rs1, id_1_id, r_1_rd, r_1_rs1, r_1_rs2, s_1_rs1, s_1_rs2, sb_1_rs1, sb_1_rs2,
       u_1_rd, uj_1_rd;
  wire [6:0] r_1_func7;
  wire [31:0] i_1_imm, s_1_imm, sb_1_imm, u_1_imm, uj_1_imm;

  ID id_1 (.opcIn(Data[6:0]), .opcOut(opcode), .ID(id_1_id));
  Decoder_part #(.select(5), .enable("false")) decoder_1 (
    .out0(decoder_1_out0), .out3(decoder_1_out3), .out4(decoder_1_out4), .out5(decoder_1_out5),
    .out6(decoder_1_out6), .out8(decoder_1_out8), .out12(decoder_1_out12), .out13(decoder_1_out13),
    .out14(decoder_1_out14), .out24(decoder_1_out24), .out25(decoder_1_out25), .out27(decoder_1_out27),
    .out28(decoder_1_out28), .sel(id_1_id));  // open: out1, out2, out7, out9, out10, out11, out15, out16, out17, out18, out19, out20, out21, out22, out23, out26, out29, out30, out31
  or or_1 (or_1_out, decoder_1_out0, decoder_1_out3, decoder_1_out4, decoder_1_out6, decoder_1_out25, decoder_1_out28);
  or or_2 (or_2_out, decoder_1_out12, decoder_1_out14);
  or or_3 (or_3_out, decoder_1_out5, decoder_1_out13);
  I i_1 (.Data(Data[31:7]), .Enable(or_1_out), .rd(i_1_rd), .func3(i_1_func3), .rs1(i_1_rs1), .imm(i_1_imm));
  S s_1 (.Data(Data[31:7]), .Enable(decoder_1_out8), .func3(s_1_func3), .rs1(s_1_rs1), .rs2(s_1_rs2), .imm(s_1_imm));
  R r_1 (
    .Data(Data[31:7]), .Enable(or_2_out), .rd(r_1_rd), .func3(r_1_func3), .rs1(r_1_rs1), .rs2(r_1_rs2),
    .func7(r_1_func7));
  U u_1 (.Data(Data[31:7]), .Enable(or_3_out), .rd(u_1_rd), .imm(u_1_imm));
  SB sb_1 (
    .Data(Data[31:7]), .Enable(decoder_1_out24), .func3(sb_1_func3), .rs1(sb_1_rs1), .rs2(sb_1_rs2),
    .imm(sb_1_imm));
  UJ uj_1 (.Data(Data[31:7]), .Enable(decoder_1_out27), .rd(uj_1_rd), .imm(uj_1_imm));
  Multiplexer #(.select(5), .width(5)) multiplexer_1 (
    .in0(i_1_rd), .in3(i_1_rd), .in4(i_1_rd), .in5(u_1_rd), .in6(i_1_rd), .in12(r_1_rd), .in13(u_1_rd),
    .in14(r_1_rd), .in25(i_1_rd), .in27(uj_1_rd), .in28(i_1_rd), .out(rd), .sel(id_1_id), .en(or_4_out));  // open: in1, in2, in7, in8, in9, in10, in11, in15, in16, in17, in18, in19, in20, in21, in22, in23, in24, in26, in29, in30, in31
  Multiplexer #(.select(5), .width(3)) multiplexer_2 (
    .in0(i_1_func3), .in3(i_1_func3), .in4(i_1_func3), .in6(i_1_func3), .in8(s_1_func3), .in12(r_1_func3),
    .in14(r_1_func3), .in24(sb_1_func3), .in25(i_1_func3), .in28(i_1_func3), .out(func3), .sel(id_1_id),
    .en(or_5_out));  // open: in1, in2, in5, in7, in9, in10, in11, in13, in15, in16, in17, in18, in19, in20, in21, in22, in23, in26, in27, in29, in30, in31
  Multiplexer #(.select(5), .width(5)) multiplexer_3 (
    .in0(i_1_rs1), .in3(i_1_rs1), .in4(i_1_rs1), .in6(i_1_rs1), .in8(s_1_rs1), .in12(r_1_rs1),
    .in14(r_1_rs1), .in24(sb_1_rs1), .in25(i_1_rs1), .in28(i_1_rs1), .out(rs1), .sel(id_1_id), .en(or_6_out));  // open: in1, in2, in5, in7, in9, in10, in11, in13, in15, in16, in17, in18, in19, in20, in21, in22, in23, in26, in27, in29, in30, in31
  Multiplexer #(.select(5), .width(5)) multiplexer_4 (
    .in8(s_1_rs2), .in12(r_1_rs2), .in14(r_1_rs2), .in24(sb_1_rs2), .out(rs2), .sel(id_1_id), .en(or_7_out));  // open: in0, in1, in2, in3, in4, in5, in6, in7, in9, in10, in11, in13, in15, in16, in17, in18, in19, in20, in21, in22, in23, in25, in26, in27, in28, in29, in30, in31
  Multiplexer #(.select(4), .width(7)) multiplexer_5 (
    .in12(r_1_func7), .in14(r_1_func7), .out(func7), .sel(bit_extender_1_out), .en(or_2_out));  // open: in0, in1, in2, in3, in4, in5, in6, in7, in8, in9, in10, in11, in13, in15
  Multiplexer #(.select(5), .width(32)) multiplexer_6 (
    .in0(i_1_imm), .in3(i_1_imm), .in4(i_1_imm), .in5(u_1_imm), .in6(i_1_imm), .in8(s_1_imm), .in13(u_1_imm),
    .in24(sb_1_imm), .in25(i_1_imm), .in27(uj_1_imm), .in28(i_1_imm), .out(imm), .sel(id_1_id), .en(or_8_out));  // open: in1, in2, in7, in9, in10, in11, in12, in14, in15, in16, in17, in18, in19, in20, in21, in22, in23, in26, in29, in30, in31
  or or_4 (or_4_out, decoder_1_out27, or_3_out, or_2_out, or_1_out);
  or or_5 (or_5_out, decoder_1_out24, or_2_out, decoder_1_out8, or_1_out);
  or or_6 (or_6_out, decoder_1_out24, or_2_out, decoder_1_out8, or_1_out);
  or or_7 (or_7_out, decoder_1_out24, or_2_out, decoder_1_out8);
  Bit_Extender #(.in_width(5), .out_width(4)) bit_extender_1 (.in(id_1_id), .out(bit_extender_1_out));
  or or_8 (or_8_out, decoder_1_out27, decoder_1_out24, or_3_out, decoder_1_out8, or_1_out);
endmodule

module ID (
  input  [6:0] opcIn,
  output [6:0] opcOut,
  output [4:0] ID
);


  assign ID = opcIn[6:2];
  assign opcOut = opcIn;
endmodule

module R (
  input  [24:0] Data,
  input  Enable,
  output [4:0] rd,
  output [2:0] func3,
  output [4:0] rs1,
  output [4:0] rs2,
  output [6:0] func7
);

  wire not_1_out;

  not not_1 (not_1_out, Enable);
  BitSelector #(.width(25), .group(25)) bitselector_1 (.in(Data), .out({func7, rs2, rs1, func3, rd}), .sel(not_1_out));
endmodule

module I (
  input  [24:0] Data,
  input  Enable,
  output [4:0] rd,
  output [2:0] func3,
  output [4:0] rs1,
  output [31:0] imm
);

  wire not_1_out;
  wire [24:13] bitselector_1_out;

  not not_1 (not_1_out, Enable);
  BitSelector #(.width(25), .group(25)) bitselector_1 (
    .in(Data), .out({bitselector_1_out, rs1, func3, rd}), .sel(not_1_out));
  assign imm = {{20{bitselector_1_out[24]}}, bitselector_1_out};  // Bit_Extender bit_extender_1
endmodule

module S (
  input  [24:0] Data,
  input  Enable,
  output [2:0] func3,
  output [4:0] rs1,
  output [4:0] rs2,
  output [31:0] imm
);

  wire not_1_out;
  wire [24:0] bitselector_1_out;

  BitSelector #(.width(25), .group(25)) bitselector_1 (
    .in(Data), .out({bitselector_1_out[24:18], rs2, rs1, func3, bitselector_1_out[4:0]}), .sel(not_1_out));
  not not_1 (not_1_out, Enable);
  assign imm = {{20{bitselector_1_out[24]}}, {bitselector_1_out[24:18], bitselector_1_out[4:0]}};  // Bit_Extender bit_extender_1
endmodule

module SB (
  input  [24:0] Data,
  input  Enable,
  output [2:0] func3,
  output [4:0] rs1,
  output [4:0] rs2,
  output [31:0] imm
);

  wire not_1_out;
  wire [24:0] bitselector_1_out;

  BitSelector #(.width(25), .group(25)) bitselector_1 (
    .in(Data), .out({bitselector_1_out[24:18], rs2, rs1, func3, bitselector_1_out[4:0]}), .sel(not_1_out));
  not not_1 (not_1_out, Enable);
  assign imm = {{19{bitselector_1_out[24]}}, {bitselector_1_out[24], bitselector_1_out[0], bitselector_1_out[23:18], bitselector_1_out[4:1], 1'b0}};  // Bit_Extender bit_extender_1
endmodule

module U (
  input  [24:0] Data,
  input  Enable,
  output [4:0] rd,
  output [31:0] imm
);

  wire not_1_out;
  wire [24:5] bitselector_1_out;

  BitSelector #(.width(25), .group(25)) bitselector_1 (.in(Data), .out({bitselector_1_out, rd}), .sel(not_1_out));
  not not_1 (not_1_out, Enable);
  assign imm = {{12{bitselector_1_out[24]}}, bitselector_1_out};  // Bit_Extender bit_extender_1
endmodule

module UJ (
  input  [24:0] Data,
  input  Enable,
  output [4:0] rd,
  output [31:0] imm
);

  wire not_1_out;
  wire [24:5] bitselector_1_out;

  BitSelector #(.width(25), .group(25)) bitselector_1 (.in(Data), .out({bitselector_1_out, rd}), .sel(not_1_out));
  not not_1 (not_1_out, Enable);
  assign imm = {{11{bitselector_1_out[24]}}, {bitselector_1_out[24], bitselector_1_out[12:5], bitselector_1_out[13], bitselector_1_out[23:14], 1'b0}};  // Bit_Extender bit_extender_1
endmodule

module Test (
  input  [31:0] Data,
  output [6:0] opcode,
  output [4:0] rd,
  output [2:0] func3,
  output [4:0] rs1,
  output [4:0] rs2,
  output [6:0] func7,
  output [31:0] imm
);

  Decoder decoder_1 (
    .Data(Data), .opcode(opcode), .rd(rd), .func3(func3), .rs1(rs1), .rs2(rs2), .func7(func7), .imm(imm));
endmodule
