// Logisim project Fetch.circ as structural Verilog: 2 circuits, main circuit Fetch
module Fetch (
  input  Reset,
  output [31:0] Output
);

  wire Clock_out;
  wire [31:0] adder_1_out, register_1_q;

  Clock Clock (.out(Clock_out));
  Register #(.width(32)) register_1 (.D(adder_1_out), .Q(register_1_q), .clk(Clock_out), .clr(Reset));  // open: en
  Adder #(.width(32)) adder_1 (.a(32'h4), .b(register_1_q), .out(adder_1_out));  // open: cin, cout
  ROM #(.addrWidth(24), .dataWidth(32)) rom_1 (.addr(register_1_q[25:2]), .data(Output));  // open: sel

  // Notes on the sheet:
  //   contents of rom_1 (hex, n*v repeats v):
  //   1543
endmodule

module Test (
  input  Reset,
  output [31:0] Output_Data
);

  Fetch fetch_1 (.Reset(Reset), .Output(Output_Data));
endmodule
