// Logisim project Load-Store.circ as structural Verilog: 1 circuit, main circuit main
module main (
  input  Write_Back_En,
  input  [31:0] inst_Input,
  input  Reset,
  output [31:0] rs1_Output,
  output [31:0] rd_Output,
  output [31:0] rs2_Output,
  output [31:0] rs2_Output_2
);

  wire Clock_out, Controller_load_en, Controller_save_en;
  wire [2:0] Decoder_func3;
  wire [4:0] Decoder_rd, Decoder_rs1, Decoder_rs2, op2ID_id;
  wire [6:0] Decoder_func7, Decoder_opcode;
  wire [31:0] ALU_rd, multiplexer_1_out, op2Sel_p4, undriven;

  Decoder Decoder (
    .Data(inst_Input), .opcode(Decoder_opcode), .rd(Decoder_rd), .func3(Decoder_func3), .rs1(Decoder_rs1),
    .rs2(Decoder_rs2), .func7(Decoder_func7), .imm(rs2_Output_2));
  ID op2ID (.opcIn(Decoder_opcode), .ID(op2ID_id));  // open: opcOut
  Multiplexer #(.width(32), .enable("false")) multiplexer_1 (
    .in0(rd_Output), .in1(undriven), .out(multiplexer_1_out), .sel(Write_Back_En));
  Register_File RegFile (
    .Write_Input(undriven), .Write_Address(Decoder_rd), .Read_Data_1(rs1_Output),
    .Read_Address_1(Decoder_rs1), .Read_Data_2(rs2_Output), .Read_Address_2(Decoder_rs2));
  // Operand_Sel op2Sel: pin names not known; wires that end beside it: rs2_Output, rs2_Output_2, op2ID_id, op2Sel_p4
  ALU ALU (.rs1(rs1_Output), .rs2_imm(op2Sel_p4), .opSel({Decoder_func7[5], Decoder_func3}), .rd(ALU_rd));
  Clock Clock (.out(Clock_out));
  Controller_main Controller (.opcIn(op2ID_id), .Load_En(Controller_load_en), .Save_En(Controller_save_en));
  RAM #(.addrWidth(24), .dataWidth(32), .bus("separate")) ram_1 (
    .addr(ALU_rd[23:0]), .din(rs2_Output), .data(multiplexer_1_out), .str(Controller_save_en), .sel(1'b1),
    .clk(Clock_out), .ld(Controller_load_en), .clr(Reset));

  // Notes on the sheet:
  //   opc
  //   rd
  //   f3
  //   rs1
  //   rs2
  //   f7
  //   imm
  //   r data 1
  //   r addr 1
  //   r data 2
  //   r addr 2
endmodule
