// Logisim project 2-Bit MUX.circ as structural Verilog: 2 circuits, main circuit main
module main (
  input  in0,
  input  in1,
  input  Select,
  output out
);

  wire nand_1_out, nand_2_out, not_1_out;

  not not_1 (not_1_out, Select);
  nand nand_1 (nand_1_out, in0, not_1_out);
  nand nand_2 (nand_2_out, Select, in1);
  nand nand_3 (out, nand_1_out, nand_2_out);
endmodule

module Test (
  input  in0,
  input  in1,
  input  Select,
  output out
);

  main main_1 (.in0(in0), .in1(in1), .Select(Select), .out(out));
endmodule
