// Logisim project 4-Bit MUX.circ as structural Verilog: 2 circuits, main circuit 4-Bit MUX
module _4_Bit_MUX (
  input  in0,
  input  in1,
  input  in2,
  input  in3,
  input  Select1,
  input  Select0,
  output out
);

  wire and_1_out, and_2_out, and_3_out, and_4_out, and_5_out, and_6_out, and_7_out, and_8_out, not_1_out,
       not_2_out, not_3_out, not_4_out, or_1_out, or_2_out;

  not not_1 (not_1_out, Select1);
  not not_2 (not_2_out, Select1);
  and and_1 (and_1_out, in0, not_1_out);
  and and_2 (and_2_out, in1, not_2_out);
  and and_3 (and_3_out, Select1, in2);
  and and_4 (and_4_out, Select1, in3);
  and and_5 (and_5_out, and_1_out, not_3_out);
  not not_3 (not_3_out, Select0);
  and and_6 (and_6_out, and_2_out, Select0);
  and and_7 (and_7_out, and_3_out, not_4_out);
  not not_4 (not_4_out, Select0);
  and and_8 (and_8_out, and_4_out, Select0);
  or or_1 (or_1_out, and_5_out, and_6_out);
  or or_2 (or_2_out, and_7_out, and_8_out);
  or or_3 (out, or_1_out, or_2_out);
endmodule

module Test (
  input  in0,
  input  in1,
  input  in2,
  input  in3,
  input  Select1,
  input  Select0,
  output out
);

  _4_Bit_MUX u_4_bit_mux_1 (
    .in0(in0), .in1(in1), .in2(in2), .in3(in3), .Select1(Select1), .Select0(Select0), .out(out));
endmodule
