// Logisim project AND-OR-NAND-NOR.circ as structural Verilog: 5 circuits, main circuit Test
module Test (
  input  in1,
  input  in2,
  output out_AND,
  output out_OR,
  output out_NAND,
  output out_NOR
);

  AND AND (.in1(in1), .in2(in2), .out(out_AND));
  OR OR (.in1(in2), .in2(in1), .out(out_OR));
  NAND NAND (.in1(in2), .in2(in1), .out(out_NAND));
  NOR NOR (.in1(in2), .in2(in1), .out(out_NOR));
endmodule

module AND (
  input  in1,
  input  in2,
  output out
);

  wire transistor_1_out;

  Transistor #(.\type ("n")) transistor_1 (.in(1'b1), .out(transistor_1_out), .gate(in1));
  Transistor #(.\type ("n")) transistor_2 (.in(transistor_1_out), .out(out), .gate(in2));
  Transistor transistor_3 (.in(1'b0), .out(out), .gate(in1));
  Transistor transistor_4 (.in(1'b0), .out(out), .gate(in2));
endmodule

module OR (
  input  in1,
  input  in2,
  output out
);

  wire transistor_1_out;

  Transistor transistor_1 (.in(1'b0), .out(transistor_1_out), .gate(in1));
  Transistor transistor_2 (.in(transistor_1_out), .out(out), .gate(in2));
  Transistor #(.\type ("n")) transistor_3 (.in(1'b1), .out(out), .gate(in1));
  Transistor #(.\type ("n")) transistor_4 (.in(1'b1), .out(out), .gate(in2));
endmodule

module NAND (
  input  in1,
  input  in2,
  output out
);

  wire transistor_1_out;

  Transistor #(.\type ("n")) transistor_1 (.in(1'b0), .out(transistor_1_out), .gate(in1));
  Transistor #(.\type ("n")) transistor_2 (.in(transistor_1_out), .out(out), .gate(in2));
  Transistor transistor_3 (.in(1'b1), .out(out), .gate(in1));
  Transistor transistor_4 (.in(1'b1), .out(out), .gate(in2));
endmodule

module NOR (
  input  in1,
  input  in2,
  output out
);

  wire transistor_1_out;

  Transistor transistor_1 (.in(1'b1), .out(transistor_1_out), .gate(in1));
  Transistor transistor_2 (.in(transistor_1_out), .out(out), .gate(in2));
  Transistor #(.\type ("n")) transistor_3 (.in(1'b0), .out(out), .gate(in1));
  Transistor #(.\type ("n")) transistor_4 (.in(1'b0), .out(out), .gate(in2));
endmodule
