// Logisim project Comparator.circ as structural Verilog: 2 circuits, main circuit Comparator
module Comparator (
  input  op1,
  input  op2,
  output op1_op2,
  output op1_op2_2,
  output op1_op2_3
);

  wire not_1_out, not_2_out;

  not not_1 (not_1_out, op1);
  not not_2 (not_2_out, op2);
  and and_1 (op1_op2, op2, not_1_out);
  xnor xnor_1 (op1_op2_2, op1, op2);
  and and_2 (op1_op2_3, not_2_out, op1);
endmodule

module Test (
  input  op1,
  input  op2,
  output op1_op2,
  output op1_op2_2,
  output op1_op2_3
);

  Comparator Comparator (.op1(op1), .op2(op2), .op1_op2(op1_op2), .op1_op2_2(op1_op2_2), .op1_op2_3(op1_op2_3));
endmodule
