// Logisim project D-Flip Flop.circ as structural Verilog: 3 circuits, main circuit D-Flip Flop
module D_Flip_Flop (
  input  D,
  input  Clk,
  output Q
);

  wire nand_1_out, nand_2_out, nand_4_out;

  nand nand_1 (nand_1_out, D, Clk);
  nand nand_2 (nand_2_out, nand_1_out, Clk);
  nand nand_3 (Q, nand_1_out, nand_4_out);
  nand nand_4 (nand_4_out, nand_2_out, Q);
endmodule

module Series (
  input  D,
  output Q0,
  output Q1,
  output Q2,
  output Q3
);

  wire clock_1_out;

  D_Flip_Flop d_flip_flop_1 (.D(D), .Clk(clock_1_out), .Q(Q0));
  Clock clock_1 (.out(clock_1_out));
  D_Flip_Flop d_flip_flop_2 (.D(Q0), .Clk(clock_1_out), .Q(Q1));
  D_Flip_Flop d_flip_flop_3 (.D(Q1), .Clk(clock_1_out), .Q(Q2));
  D_Flip_Flop d_flip_flop_4 (.D(Q2), .Clk(clock_1_out), .Q(Q3));
endmodule

module Parallel (
  input  D0,
  input  D1,
  input  D2,
  input  D3,
  output Q0,
  output Q1,
  output Q2,
  output Q3
);

  wire clock_1_out;

  Clock clock_1 (.out(clock_1_out));
  D_Flip_Flop d_flip_flop_1 (.D(D0), .Clk(clock_1_out), .Q(Q0));
  D_Flip_Flop d_flip_flop_2 (.D(D1), .Clk(clock_1_out), .Q(Q1));
  D_Flip_Flop d_flip_flop_3 (.D(D2), .Clk(clock_1_out), .Q(Q2));
  D_Flip_Flop d_flip_flop_4 (.D(D3), .Clk(clock_1_out), .Q(Q3));
endmodule
