// Logisim project Full-Adder.circ as structural Verilog: 2 circuits, main circuit Full-Adder
module Full_Adder (
  input  op1,
  input  op2,
  input  CIn,
  output COut,
  output Sum
);

  wire and_1_out, and_2_out, xor_1_out;

  xor xor_1 (xor_1_out, op1, op2);
  xor xor_2 (Sum, xor_1_out, CIn);
  and and_1 (and_1_out, xor_1_out, CIn);
  and and_2 (and_2_out, op2, op1);
  or or_1 (COut, and_1_out, and_2_out);
endmodule

module Test (
  input  op1,
  input  op2,
  input  CIn,
  output COut,
  output Sum
);

  Full_Adder Full_Adder (.op1(op1), .op2(op2), .CIn(CIn), .COut(COut), .Sum(Sum));
endmodule
