// Logisim project Half-Adder.circ as structural Verilog: 2 circuits, main circuit Half-Adder
module Half_Adder (
  input  op1,
  input  op2,
  output Carry,
  output Sum
);

  xor xor_1 (Sum, op1, op2);
  and and_1 (Carry, op2, op1);
endmodule

module Test (
  input  op1,
  input  op2,
  input  Carry,
  input  Sum
);

  Half_Adder Half_Adder (.op1(op1), .op2(op2), .Carry(Carry), .Sum(Sum));
endmodule
