// Logisim project SR-Latch.circ as structural Verilog: 2 circuits, main circuit SR-Latch
module SR_Latch (
  input  Reset,
  input  Set,
  output Q,
  output nQ
);

  nor nor_1 (Q, Reset, nQ);
  nor nor_2 (nQ, Q, Set);
endmodule

module Test (
  input  Reset,
  input  Set,
  output Q,
  output nQ
);

  SR_Latch SR_Latch (.Reset(Reset), .Set(Set), .Q(Q), .nQ(nQ));
endmodule
