// Logisim project CPU Core.circ as structural Verilog: 6 circuits, main circuit Core
module Core (
  output [31:0] Loaded_data_not_saved_to_RegFile,
  output [31:0] fetched_inst
);

  wire clk_out, controller_1_jal, controller_1_load_en, controller_1_store_en;
  wire [2:0] decoder_1_func3;
  wire [4:0] decoder_1_id_out, decoder_1_rd, decoder_1_rs1, decoder_1_rs2;
  wire [6:0] decoder_1_func7;
  wire [31:0] alu_1_out, decoder_1_imm, fetch_1_pc_out, jal_1_npc_out, or_1_out, RegFile_rs1_data,
       RegFile_rs2_data, undriven;

  Clock clk (.out(clk_out));
  Fetch fetch_1 (
    .inst_out(fetched_inst), .clk(clk_out), .nextPC(jal_1_npc_out), .jal_en(controller_1_jal),
    .PC_out(fetch_1_pc_out));  // open: reset
  Decoder decoder_1 (
    .inst_in(fetched_inst), .rd(decoder_1_rd), .func3(decoder_1_func3), .rs1(decoder_1_rs1),
    .rs2(decoder_1_rs2), .func7(decoder_1_func7), .imm(decoder_1_imm), .ID_out(decoder_1_id_out));  // open: opcode
  Register_File RegFile (
    .write_in(undriven), .clk(clk_out), .rs1_data(RegFile_rs1_data), .rs1_addr(decoder_1_rs1),
    .rs2_data(RegFile_rs2_data), .rs2_addr(decoder_1_rs2), .write_addr(decoder_1_rd));
  assign or_1_out = RegFile_rs2_data | decoder_1_imm;  // OR_Gate or_1, 32 bits wide
  ALU alu_1 (
    .rs1_data(RegFile_rs1_data), .rs2_imm_data(or_1_out), .out(alu_1_out), .func3(decoder_1_func3),
    .func7(decoder_1_func7), .ID(decoder_1_id_out));
  jal jal_1 (.PC_in(fetch_1_pc_out), .imm(or_1_out), .nPC_out(jal_1_npc_out));
  Controller controller_1 (
    .ID(decoder_1_id_out), .store_en(controller_1_store_en), .load_en(controller_1_load_en),
    .jal(controller_1_jal));
  RAM #(.addrWidth(24), .dataWidth(32), .bus("separate")) ram_1 (
    .addr(alu_1_out[23:0]), .din(RegFile_rs2_data), .data(Loaded_data_not_saved_to_RegFile),
    .str(controller_1_store_en), .sel(1'b1), .clk(clk_out), .ld(controller_1_load_en));  // open: clr
endmodule

module rs2_imm_Generator (
  input  [31:0] rs2_data,
  input  [31:0] imm,
  input  [4:0] ID,
  output [31:0] out
);

  Multiplexer #(.select(2), .width(32), .enable("false")) multiplexer_1 (
    .in1(imm), .in2(rs2_data), .in3(rs2_data), .out(out), .sel(ID[3:2]));  // open: in0
endmodule

module nextPC (
  input  in_1
);
endmodule

module jal (
  input  [31:0] PC_in,
  input  [31:0] imm,
  output [31:0] nPC_out
);

  wire [31:0] shifter_1_out;

  Adder #(.width(32)) adder_1 (.a(PC_in), .b(shifter_1_out), .out(nPC_out));  // open: cin, cout
  Shifter #(.width(32)) shifter_1 (.in(imm), .\dist (5'b00001), .out(shifter_1_out));
endmodule

module Test (
  input  reset,
  output [31:0] Loaded_data,
  output [31:0] fetched_inst
);

  wire clk_out, controller_1_jal, controller_1_load_en, controller_1_store_en;
  wire [2:0] decoder_1_func3;
  wire [4:0] decoder_1_id_out, decoder_1_rd, decoder_1_rs1, decoder_1_rs2;
  wire [6:0] decoder_1_func7;
  wire [31:0] adder_1_out, alu_1_out, decoder_1_imm, jal_1_npc_out, or_1_out, PC_q, RegFile_rs1_data,
       RegFile_rs2_data;

  Multiplexer #(.width(32), .enable("false")) multiplexer_1 (
    .in1(jal_1_npc_out), .sel(controller_1_jal));  // open: in0, out
  Register #(.width(32)) PC (.D(adder_1_out), .Q(PC_q), .clk(clk_out), .clr(reset));  // open: en
  Adder #(.width(32)) adder_1 (.a(32'h4), .b(PC_q), .out(adder_1_out));  // open: cin, cout
  Clock clk (.out(clk_out));
  RAM #(.addrWidth(24), .dataWidth(32), .bus("asynch")) ram_1 (
    .addr(PC_q[25:2]), .data(fetched_inst));  // open: sel, ld, clr
  Decoder decoder_1 (
    .inst_in(fetched_inst), .rd(decoder_1_rd), .func3(decoder_1_func3), .rs1(decoder_1_rs1),
    .rs2(decoder_1_rs2), .func7(decoder_1_func7), .imm(decoder_1_imm), .ID_out(decoder_1_id_out));  // open: opcode
  Register_File RegFile (
    .write_in(Loaded_data), .clk(clk_out), .rs1_data(RegFile_rs1_data), .rs1_addr(decoder_1_rs1),
    .rs2_data(RegFile_rs2_data), .rs2_addr(decoder_1_rs2), .write_addr(decoder_1_rd));
  assign or_1_out = RegFile_rs2_data | decoder_1_imm;  // OR_Gate or_1, 32 bits wide
  ALU alu_1 (
    .rs1_data(RegFile_rs1_data), .rs2_imm_data(or_1_out), .out(alu_1_out), .func3(decoder_1_func3),
    .func7(decoder_1_func7), .ID(decoder_1_id_out));
  Controller controller_1 (
    .ID(decoder_1_id_out), .store_en(controller_1_store_en), .load_en(controller_1_load_en),
    .jal(controller_1_jal));
  jal jal_1 (.PC_in(PC_q), .imm(or_1_out), .nPC_out(jal_1_npc_out));
  RAM #(.addrWidth(24), .dataWidth(32), .bus("separate")) ram_2 (
    .addr(alu_1_out[23:0]), .din(RegFile_rs2_data), .data(Loaded_data), .str(controller_1_store_en),
    .sel(1'b1), .clk(clk_out), .ld(controller_1_load_en));  // open: clr
endmodule

module rd_Sel (
  input  [4:0] rd,
  input  jal_en,
  output [4:0] out
);

  Multiplexer #(.width(5), .enable("false")) multiplexer_1 (.in0(rd), .in1(5'b00001), .out(out), .sel(jal_en));
endmodule
