// Logisim project Controller.circ as structural Verilog: 1 circuit, main circuit Controller
module Controller (
  input  [4:0] ID,
  output store_en,
  output load_en,
  output reg_en
);

  wire comparator_3_eq;

  Comparator #(.width(3), .mode("unsigned")) comparator_1 (.a(3'b010), .b(ID[4:2]), .eq(store_en));  // open: gt, lt
  Comparator #(.width(5), .mode("unsigned")) comparator_2 (.a({5{1'b0}}), .b(ID), .eq(load_en));  // open: gt, lt
  Comparator #(.width(5), .mode("unsigned")) comparator_3 (.a(ID), .b(5'b01100), .eq(comparator_3_eq));  // open: gt, lt
  or or_1 (reg_en, load_en, comparator_3_eq);
endmodule
