// Logisim project Decoder.circ as structural Verilog: 8 circuits, main circuit Decoder
module Decoder (
  input  [31:0] inst_in,
  output [6:0] opcode,
  output [4:0] rd,
  output [2:0] func3,
  output [4:0] rs1,
  output [4:0] rs2,
  output [6:0] func7,
  output [31:0] imm,
  output [4:0] ID_out
);

  wire Type_ID_i_type_en, Type_ID_r_type_en, Type_ID_s_type_en, Type_ID_sb_type_en, Type_ID_u_type_en,
       Type_ID_uj_type_en;
  wire [2:0] I_func3, R_func3, S_func3, SB_func3;
  wire [4:0] I_rd, I_rs1, R_rd, R_rs1, R_rs2, S_rs1, S_rs2, SB_rs1, SB_rs2, U_rd, UJ_p3;
  wire [31:0] I_imm, S_imm, SB_imm, U_imm, UJ_p4;

  Type_ID Type_ID (
    .opc_in(inst_in[6:0]), .opc_out(opcode), .I_Type_en(Type_ID_i_type_en), .S_Type_en(Type_ID_s_type_en),
    .U_Type_en(Type_ID_u_type_en), .R_Type_en(Type_ID_r_type_en), .SB_Type_en(Type_ID_sb_type_en),
    .UJ_Type_en(Type_ID_uj_type_en), .ID_out(ID_out));
  I_Type I (.in(inst_in[31:7]), .en(Type_ID_i_type_en), .rd(I_rd), .func3(I_func3), .rs1(I_rs1), .imm(I_imm));
  S_Type S (.in(inst_in[31:7]), .en(Type_ID_s_type_en), .func3(S_func3), .rs1(S_rs1), .rs2(S_rs2), .imm(S_imm));
  U_Type U (.in(inst_in[31:7]), .en(Type_ID_u_type_en), .rd(U_rd), .imm(U_imm));
  R_Type R (
    .in(inst_in[31:7]), .en(Type_ID_r_type_en), .rd(R_rd), .func3(R_func3), .rs1(R_rs1), .rs2(R_rs2),
    .func7(func7));
  SB_Type SB (.in(inst_in[31:7]), .en(Type_ID_sb_type_en), .func3(SB_func3), .rs1(SB_rs1), .rs2(SB_rs2), .imm(SB_imm));
  // UJ_Type UJ: pin names not known; wires that end beside it: inst_in[31:7], Type_ID_uj_type_en, UJ_p3, UJ_p4
  assign rd = I_rd | U_rd | R_rd | UJ_p3;  // OR_Gate or_1, 5 bits wide
  assign func3 = I_func3 | S_func3 | R_func3 | SB_func3;  // OR_Gate or_2, 3 bits wide
  assign rs1 = I_rs1 | S_rs1 | R_rs1 | SB_rs1;  // OR_Gate or_3, 5 bits wide
  assign rs2 = S_rs2 | R_rs2 | SB_rs2;  // OR_Gate or_4, 5 bits wide
  assign imm = I_imm | S_imm | U_imm | SB_imm | UJ_p4;  // OR_Gate or_5, 32 bits wide
endmodule

module Type_ID (
  input  [6:0] opc_in,
  output [6:0] opc_out,
  output I_Type_en,
  output S_Type_en,
  output U_Type_en,
  output R_Type_en,
  output SB_Type_en,
  output UJ_Type_en,
  output [4:0] ID_out
);

  wire decoder_1_out0, decoder_1_out3, decoder_1_out4, decoder_1_out5, decoder_1_out6, decoder_1_out12,
       decoder_1_out13, decoder_1_out14, decoder_1_out25, decoder_1_out28;

  Decoder_part #(.select(5), .enable("false")) decoder_1 (
    .out0(decoder_1_out0), .out3(decoder_1_out3), .out4(decoder_1_out4), .out5(decoder_1_out5),
    .out6(decoder_1_out6), .out8(S_Type_en), .out12(decoder_1_out12), .out13(decoder_1_out13),
    .out14(decoder_1_out14), .out24(SB_Type_en), .out25(decoder_1_out25), .out27(UJ_Type_en),
    .out28(decoder_1_out28), .sel(opc_in[6:2]));  // open: out1, out2, out7, out9, out10, out11, out15, out16, out17, out18, out19, out20, out21, out22, out23, out26, out29, out30, out31
  or or_1 (I_Type_en, decoder_1_out0, decoder_1_out3, decoder_1_out4, decoder_1_out6, decoder_1_out25, decoder_1_out28);
  or or_2 (U_Type_en, decoder_1_out5, decoder_1_out13);
  or or_3 (R_Type_en, decoder_1_out14, decoder_1_out12);

  assign ID_out = opc_in[6:2];
  assign opc_out = opc_in;
endmodule

module R_Type (
  input  [24:0] in,
  input  en,
  output [4:0] rd,
  output [2:0] func3,
  output [4:0] rs1,
  output [4:0] rs2,
  output [6:0] func7
);

  wire not_1_out;

  not not_1 (not_1_out, en);
  BitSelector #(.width(25), .group(25)) bitselector_1 (.in(in), .out({func7, rs2, rs1, func3, rd}), .sel(not_1_out));
endmodule

module I_Type (
  input  [24:0] in,
  input  en,
  output [4:0] rd,
  output [2:0] func3,
  output [4:0] rs1,
  output [31:0] imm
);

  wire not_1_out;
  wire [24:13] bitselector_1_out;

  not not_1 (not_1_out, en);
  BitSelector #(.width(25), .group(25)) bitselector_1 (
    .in(in), .out({bitselector_1_out, rs1, func3, rd}), .sel(not_1_out));
  assign imm = {{20{bitselector_1_out[24]}}, bitselector_1_out};  // Bit_Extender bit_extender_1
endmodule

module S_Type (
  input  [24:0] in,
  input  en,
  output [2:0] func3,
  output [4:0] rs1,
  output [4:0] rs2,
  output [31:0] imm
);

  wire not_1_out;
  wire [24:0] bitselector_1_out;

  not not_1 (not_1_out, en);
  BitSelector #(.width(25), .group(25)) bitselector_1 (
    .in(in), .out({bitselector_1_out[24:18], rs2, rs1, func3, bitselector_1_out[4:0]}), .sel(not_1_out));
  assign imm = {{20{bitselector_1_out[24]}}, {bitselector_1_out[24:18], bitselector_1_out[4:0]}};  // Bit_Extender bit_extender_1
endmodule

module SB_Type (
  input  [24:0] in,
  input  en,
  output [2:0] func3,
  output [4:0] rs1,
  output [4:0] rs2,
  output [31:0] imm
);

  wire not_1_out;
  wire [24:0] bitselector_1_out;

  not not_1 (not_1_out, en);
  BitSelector #(.width(25), .group(25)) bitselector_1 (
    .in(in), .out({bitselector_1_out[24:18], rs2, rs1, func3, bitselector_1_out[4:0]}), .sel(not_1_out));
  assign imm = {{19{bitselector_1_out[24]}}, {bitselector_1_out[24], bitselector_1_out[0], bitselector_1_out[23:18], bitselector_1_out[4:1], 1'b0}};  // Bit_Extender bit_extender_1
endmodule

module U_Type (
  input  [24:0] in,
  input  en,
  output [4:0] rd,
  output [31:0] imm
);

  wire not_1_out;
  wire [24:5] bitselector_1_out;

  BitSelector #(.width(25), .group(25)) bitselector_1 (.in(in), .out({bitselector_1_out, rd}), .sel(not_1_out));
  not not_1 (not_1_out, en);
  assign imm = {{12{bitselector_1_out[24]}}, bitselector_1_out};  // Bit_Extender bit_extender_1
endmodule

module UJ_Type (
  input  [24:0] in,
  input  en,
  output [4:0] rd,
  output [31:0] imm
);

  wire decoder_1_out1, not_1_out;
  wire [24:0] bitselector_1_out;

  not not_1 (not_1_out, en);
  BitSelector #(.width(25), .group(25)) bitselector_1 (.in(in), .out(bitselector_1_out), .sel(not_1_out));
  Decoder_part #(.enable("false")) decoder_1 (.out1(decoder_1_out1), .sel(en));  // open: out0
  assign imm = {{11{bitselector_1_out[24]}}, {bitselector_1_out[24], bitselector_1_out[12:5], bitselector_1_out[13], bitselector_1_out[23:14], 1'b0}};  // Bit_Extender bit_extender_1
  assign rd = {{4{1'b0}}, decoder_1_out1};  // Bit_Extender bit_extender_2
endmodule
