// Logisim project Fetch.circ as structural Verilog: 1 circuit, main circuit Fetch
module Fetch (
  input  [31:0] nextPC,
  input  jal_en,
  input  clk,
  input  reset,
  output [31:0] inst_out,
  output [31:0] PC_out
);

  wire [31:0] adder_1_out, multiplexer_1_out;

  Multiplexer #(.width(32), .enable("false")) multiplexer_1 (
    .in0(adder_1_out), .in1(nextPC), .out(multiplexer_1_out), .sel(jal_en));
  Register #(.width(32)) PC (.D(multiplexer_1_out), .Q(PC_out), .clk(clk), .clr(reset));  // open: en
  Adder #(.width(32)) adder_1 (.a(32'h4), .b(PC_out), .out(adder_1_out));  // open: cin, cout
  RAM #(.addrWidth(24), .dataWidth(32), .bus("asynch")) ram_1 (
    .addr(PC_out[25:2]), .data(inst_out));  // open: sel, ld, clr
endmodule
