// Logisim project Register File.circ as structural Verilog: 1 circuit, main circuit Register File
module Register_File (
  input  [31:0] write_in,
  input  clk,
  input  [4:0] rs1_addr,
  input  [4:0] write_addr,
  input  [4:0] rs2_addr,
  output [31:0] rs1_data,
  output [31:0] rs2_data
);

  wire decoder_1_out1, decoder_1_out2, decoder_1_out3, decoder_1_out4, decoder_1_out5, decoder_1_out6,
       decoder_1_out7, decoder_1_out8, decoder_1_out9, decoder_1_out10, decoder_1_out11, decoder_1_out12,
       decoder_1_out13, decoder_1_out14, decoder_1_out15, decoder_1_out16, decoder_1_out17, decoder_1_out18,
       decoder_1_out19, decoder_1_out20, decoder_1_out21, decoder_1_out22, decoder_1_out23, decoder_1_out24,
       decoder_1_out25, decoder_1_out26, decoder_1_out27, decoder_1_out28, decoder_1_out29, decoder_1_out30,
       decoder_1_out31;
  wire [31:0] x0_q, x1_q, x2_q, x3_q, x4_q, x5_q, x6_q, x7_q, x8_q, x9_q, x10_q, x11_q, x12_q, x13_q, x14_q,
       x15_q, x16_q, x17_q, x18_q, x19_q, x20_q, x21_q, x22_q, x23_q, x24_q, x25_q, x26_q, x27_q, x28_q,
       x29_q, x30_q, x31_q;

  Decoder #(.select(5), .enable("false")) decoder_1 (
    .out1(decoder_1_out1), .out2(decoder_1_out2), .out3(decoder_1_out3), .out4(decoder_1_out4),
    .out5(decoder_1_out5), .out6(decoder_1_out6), .out7(decoder_1_out7), .out8(decoder_1_out8),
    .out9(decoder_1_out9), .out10(decoder_1_out10), .out11(decoder_1_out11), .out12(decoder_1_out12),
    .out13(decoder_1_out13), .out14(decoder_1_out14), .out15(decoder_1_out15), .out16(decoder_1_out16),
    .out17(decoder_1_out17), .out18(decoder_1_out18), .out19(decoder_1_out19), .out20(decoder_1_out20),
    .out21(decoder_1_out21), .out22(decoder_1_out22), .out23(decoder_1_out23), .out24(decoder_1_out24),
    .out25(decoder_1_out25), .out26(decoder_1_out26), .out27(decoder_1_out27), .out28(decoder_1_out28),
    .out29(decoder_1_out29), .out30(decoder_1_out30), .out31(decoder_1_out31), .sel(write_addr));  // open: out0
  Register #(.width(32)) x0 (.D({32{1'b0}}), .Q(x0_q));  // open: en, clk, clr
  Register #(.width(32)) x2 (.D(write_in), .en(decoder_1_out2), .Q(x2_q), .clk(clk));  // open: clr
  Register #(.width(32)) x4 (.D(write_in), .en(decoder_1_out4), .Q(x4_q), .clk(clk));  // open: clr
  Register #(.width(32)) x6 (.D(write_in), .en(decoder_1_out6), .Q(x6_q), .clk(clk));  // open: clr
  Register #(.width(32)) x8 (.D(write_in), .en(decoder_1_out8), .Q(x8_q), .clk(clk));  // open: clr
  Register #(.width(32)) x10 (.D(write_in), .en(decoder_1_out10), .Q(x10_q), .clk(clk));  // open: clr
  Register #(.width(32)) x12 (.D(write_in), .en(decoder_1_out12), .Q(x12_q), .clk(clk));  // open: clr
  Register #(.width(32)) x14 (.D(write_in), .en(decoder_1_out14), .Q(x14_q), .clk(clk));  // open: clr
  Register #(.width(32)) x16 (.D(write_in), .en(decoder_1_out16), .Q(x16_q), .clk(clk));  // open: clr
  Register #(.width(32)) x18 (.D(write_in), .en(decoder_1_out18), .Q(x18_q), .clk(clk));  // open: clr
  Register #(.width(32)) x20 (.D(write_in), .en(decoder_1_out20), .Q(x20_q), .clk(clk));  // open: clr
  Register #(.width(32)) x22 (.D(write_in), .en(decoder_1_out22), .Q(x22_q), .clk(clk));  // open: clr
  Register #(.width(32)) x24 (.D(write_in), .en(decoder_1_out24), .Q(x24_q), .clk(clk));  // open: clr
  Register #(.width(32)) x26 (.D(write_in), .en(decoder_1_out26), .Q(x26_q), .clk(clk));  // open: clr
  Register #(.width(32)) x28 (.D(write_in), .en(decoder_1_out28), .Q(x28_q), .clk(clk));  // open: clr
  Register #(.width(32)) x30 (.D(write_in), .en(decoder_1_out30), .Q(x30_q), .clk(clk));  // open: clr
  Register #(.width(32)) x1 (.D(write_in), .en(decoder_1_out1), .Q(x1_q), .clk(clk));  // open: clr
  Register #(.width(32)) x3 (.D(write_in), .en(decoder_1_out3), .Q(x3_q), .clk(clk));  // open: clr
  Register #(.width(32)) x5 (.D(write_in), .en(decoder_1_out5), .Q(x5_q), .clk(clk));  // open: clr
  Register #(.width(32)) x7 (.D(write_in), .en(decoder_1_out7), .Q(x7_q), .clk(clk));  // open: clr
  Register #(.width(32)) x9 (.D(write_in), .en(decoder_1_out9), .Q(x9_q), .clk(clk));  // open: clr
  Register #(.width(32)) x11 (.D(write_in), .en(decoder_1_out11), .Q(x11_q), .clk(clk));  // open: clr
  Register #(.width(32)) x13 (.D(write_in), .en(decoder_1_out13), .Q(x13_q), .clk(clk));  // open: clr
  Register #(.width(32)) x15 (.D(write_in), .en(decoder_1_out15), .Q(x15_q), .clk(clk));  // open: clr
  Register #(.width(32)) x17 (.D(write_in), .en(decoder_1_out17), .Q(x17_q), .clk(clk));  // open: clr
  Register #(.width(32)) x19 (.D(write_in), .en(decoder_1_out19), .Q(x19_q), .clk(clk));  // open: clr
  Register #(.width(32)) x21 (.D(write_in), .en(decoder_1_out21), .Q(x21_q), .clk(clk));  // open: clr
  Register #(.width(32)) x23 (.D(write_in), .en(decoder_1_out23), .Q(x23_q), .clk(clk));  // open: clr
  Register #(.width(32)) x25 (.D(write_in), .en(decoder_1_out25), .Q(x25_q), .clk(clk));  // open: clr
  Register #(.width(32)) x27 (.D(write_in), .en(decoder_1_out27), .Q(x27_q), .clk(clk));  // open: clr
  Register #(.width(32)) x29 (.D(write_in), .en(decoder_1_out29), .Q(x29_q), .clk(clk));  // open: clr
  Register #(.width(32)) x31 (.D(write_in), .en(decoder_1_out31), .Q(x31_q), .clk(clk));  // open: clr
  Multiplexer #(.select(5), .width(32), .enable("false")) multiplexer_1 (
    .in0(x0_q), .in1(x1_q), .in2(x2_q), .in3(x3_q), .in4(x4_q), .in5(x5_q), .in6(x6_q), .in7(x7_q),
    .in8(x8_q), .in9(x9_q), .in10(x10_q), .in11(x11_q), .in12(x12_q), .in13(x13_q), .in14(x14_q),
    .in15(x15_q), .in16(x16_q), .in17(x17_q), .in18(x18_q), .in19(x19_q), .in20(x20_q), .in21(x21_q),
    .in22(x22_q), .in23(x23_q), .in24(x24_q), .in25(x25_q), .in26(x26_q), .in27(x27_q), .in28(x28_q),
    .in29(x29_q), .in30(x30_q), .in31(x31_q), .out(rs1_data), .sel(rs1_addr));
  Multiplexer #(.select(5), .width(32), .enable("false")) multiplexer_2 (
    .in0(x0_q), .in1(x1_q), .in2(x2_q), .in3(x3_q), .in4(x4_q), .in5(x5_q), .in6(x6_q), .in7(x7_q),
    .in8(x8_q), .in9(x9_q), .in10(x10_q), .in11(x11_q), .in12(x12_q), .in13(x13_q), .in14(x14_q),
    .in15(x15_q), .in16(x16_q), .in17(x17_q), .in18(x18_q), .in19(x19_q), .in20(x20_q), .in21(x21_q),
    .in22(x22_q), .in23(x23_q), .in24(x24_q), .in25(x25_q), .in26(x26_q), .in27(x27_q), .in28(x28_q),
    .in29(x29_q), .in30(x30_q), .in31(x31_q), .out(rs2_data), .sel(rs2_addr));
endmodule
