// Logisim project ALU.circ as structural Verilog: 2 circuits, main circuit ALU
module ALU (
  input  [31:0] rs1_data,
  input  [31:0] rs2_data,
  input  [31:0] imm,
  input  op2Sel,
  input  [2:0] func3,
  input  [6:0] func7,
  input  [4:0] ID,
  output [31:0] out
);

  wire comparator_1_eq, comparator_1_gt, comparator_1_lt, comparator_2_eq, comparator_2_gt, comparator_2_lt,
       not_1_out, or_2_out, or_3_out;
  wire [4:0] opsel_1_opsel;
  wire [31:0] adder_1_out, and_1_out, bit_extender_1_out, bit_extender_2_out, bit_extender_3_out,
       bit_extender_4_out, bit_extender_5_out, bit_extender_6_out, multiplexer_1_out, or_1_out,
       shifter_1_out, shifter_2_out, shifter_3_out, subtractor_1_out, xor_1_out;

  Multiplexer #(.width(32), .enable("false")) multiplexer_1 (
    .in0(rs2_data), .in1(imm), .out(multiplexer_1_out), .sel(op2Sel));
  Comparator #(.width(32)) comparator_1 (
    .a(rs1_data), .b(multiplexer_1_out), .gt(comparator_1_gt), .eq(comparator_1_eq), .lt(comparator_1_lt));
  Comparator #(.width(32), .mode("unsigned")) comparator_2 (
    .a(rs1_data), .b(multiplexer_1_out), .gt(comparator_2_gt), .eq(comparator_2_eq), .lt(comparator_2_lt));
  Adder #(.width(32)) adder_1 (.a(rs1_data), .b(multiplexer_1_out), .out(adder_1_out));  // open: cin, cout
  Subtractor #(.width(32)) subtractor_1 (
    .a(rs1_data), .b(multiplexer_1_out), .out(subtractor_1_out));  // open: bin, bout
  Shifter #(.width(32)) shifter_1 (.in(rs1_data), .\dist (multiplexer_1_out[4:0]), .out(shifter_1_out));
  assign xor_1_out = rs1_data ^ multiplexer_1_out;  // XOR_Gate xor_1, 32 bits wide
  Shifter #(.width(32), .shift("lr")) shifter_2 (.in(rs1_data), .\dist (multiplexer_1_out[4:0]), .out(shifter_2_out));
  Shifter #(.width(32), .shift("ar")) shifter_3 (.in(rs1_data), .\dist (multiplexer_1_out[4:0]), .out(shifter_3_out));
  assign or_1_out = rs1_data | multiplexer_1_out;  // OR_Gate or_1, 32 bits wide
  assign and_1_out = rs1_data & multiplexer_1_out;  // AND_Gate and_1, 32 bits wide
  not not_1 (not_1_out, comparator_1_eq);
  or or_2 (or_2_out, comparator_1_gt, comparator_1_eq);
  or or_3 (or_3_out, comparator_2_gt, comparator_2_eq);
  assign bit_extender_1_out = {{31{1'b0}}, comparator_1_eq};  // Bit_Extender bit_extender_1
  assign bit_extender_2_out = {{31{1'b0}}, not_1_out};  // Bit_Extender bit_extender_2
  assign bit_extender_3_out = {{31{1'b0}}, comparator_1_lt};  // Bit_Extender bit_extender_3
  assign bit_extender_4_out = {{31{1'b0}}, or_2_out};  // Bit_Extender bit_extender_4
  assign bit_extender_5_out = {{31{1'b0}}, comparator_2_lt};  // Bit_Extender bit_extender_5
  assign bit_extender_6_out = {{31{1'b0}}, or_3_out};  // Bit_Extender bit_extender_6
  opSel opsel_1 (.func3(func3), .func7(func7), .ID(ID), .opSel(opsel_1_opsel));
  Multiplexer #(.select(5), .width(32), .enable("false")) multiplexer_2 (
    .in0(bit_extender_1_out), .in1(bit_extender_2_out), .in2(adder_1_out), .in4(bit_extender_3_out),
    .in5(bit_extender_4_out), .in6(bit_extender_5_out), .in7(bit_extender_6_out), .in16(adder_1_out),
    .in17(shifter_1_out), .in18(bit_extender_3_out), .in19(bit_extender_5_out), .in20(xor_1_out),
    .in21(shifter_2_out), .in22(or_1_out), .in23(and_1_out), .in24(subtractor_1_out), .in29(shifter_3_out),
    .out(out), .sel(opsel_1_opsel));  // open: in3, in8, in9, in10, in11, in12, in13, in14, in15, in25, in26, in27, in28, in30, in31
endmodule

module opSel (
  input  [2:0] func3,
  input  [6:0] func7,
  input  [4:0] ID,
  output [4:0] opSel
);


  assign opSel = {ID[2], func7[5], func3};
endmodule
