// Logisim project CPU Core.circ as structural Verilog: 6 circuits, main circuit Core
module Core (
  input  reset
);

  wire clk_out, Control_Unit_auipc_en, Control_Unit_branch_en, Control_Unit_diverter_en, Control_Unit_jal_en,
       Control_Unit_jalr_en, Control_Unit_load_en, Control_Unit_lui_en, Control_Unit_op2sel,
       Control_Unit_store_en, or_1_out, or_2_out, Write_Type_branch_out;
  wire [2:0] Decoder_func3;
  wire [4:0] Decoder_id_out, Decoder_rd, Decoder_rs1, Decoder_rs2;
  wire [6:0] Decoder_func7;
  wire [23:0] Diverter_load_out, fetch_1_inst_out;
  wire [31:0] ALU_out, Decoder_imm, Diverter_alu_out, fetch_1_pc_out, pc_next_1_npc_out, ram_1_data,
       RegisterFile_rs1_data, RegisterFile_rs2_data, rom_1_data, U_Inst_auipc_out, U_Inst_lui_out,
       Write_Type_out;

  PC_Next pc_next_1 (
    .imm(Decoder_imm), .PC_in(fetch_1_pc_out), .rs1_in(RegisterFile_rs1_data), .nPC_out(pc_next_1_npc_out),
    .jalr_en(Control_Unit_jalr_en));
  Clock clk (.out(clk_out));
  or or_1 (or_1_out, Write_Type_branch_out, or_2_out);
  Fetch fetch_1 (
    .inst_out(fetch_1_inst_out), .clk(clk_out), .reset(reset), .nextPC(pc_next_1_npc_out), .nPC_en(or_1_out),
    .PC_out(fetch_1_pc_out));
  or or_2 (or_2_out, Control_Unit_jalr_en, Control_Unit_jal_en);
  ROM #(.addrWidth(24), .dataWidth(32)) rom_1 (.addr(fetch_1_inst_out), .data(rom_1_data), .sel(1'b1));
  U_Inst U_Inst (.imm(Decoder_imm), .PC_in(fetch_1_pc_out), .lui_out(U_Inst_lui_out), .auipc_out(U_Inst_auipc_out));
  Decoder Decoder (
    .inst_in(rom_1_data), .rd(Decoder_rd), .func3(Decoder_func3), .rs1(Decoder_rs1), .rs2(Decoder_rs2),
    .func7(Decoder_func7), .imm(Decoder_imm), .ID_out(Decoder_id_out));  // open: opcode
  Control_Unit Control_Unit (
    .ID(Decoder_id_out), .store_en(Control_Unit_store_en), .load_en(Control_Unit_load_en),
    .jal_en(Control_Unit_jal_en), .lui_en(Control_Unit_lui_en), .op2Sel(Control_Unit_op2sel),
    .branch_en(Control_Unit_branch_en), .jalr_en(Control_Unit_jalr_en), .auipc_en(Control_Unit_auipc_en),
    .Diverter_en(Control_Unit_diverter_en));
  Write_Type Write_Type (
    .ALU_in(Diverter_alu_out), .Load_in(ram_1_data), .nPC_in(fetch_1_pc_out), .auipc_in(U_Inst_auipc_out),
    .lui_in(U_Inst_lui_out), .out(Write_Type_out), .Branch_en(Control_Unit_branch_en),
    .Branch_out(Write_Type_branch_out), .Load_en(Control_Unit_load_en), .nPC_en(or_2_out),
    .auipc_en(Control_Unit_auipc_en), .lui_en(Control_Unit_lui_en));
  Register_File RegisterFile (
    .write_in(Write_Type_out), .clk(clk_out), .rs1_data(RegisterFile_rs1_data), .rs1_addr(Decoder_rs1),
    .rs2_data(RegisterFile_rs2_data), .rs2_addr(Decoder_rs2), .write_addr(Decoder_rd), .reset(reset));
  ALU ALU (
    .rs1_data(RegisterFile_rs1_data), .rs2_data(RegisterFile_rs2_data), .out(ALU_out), .func3(Decoder_func3),
    .func7(Decoder_func7), .ID(Decoder_id_out), .imm(Decoder_imm), .op2Sel(Control_Unit_op2sel));
  Diverter Diverter (
    .in(ALU_out), .Load_out(Diverter_load_out), .ALU_out(Diverter_alu_out), .en(Control_Unit_diverter_en));
  RAM #(.addrWidth(24), .dataWidth(32), .bus("separate")) ram_1 (
    .addr(Diverter_load_out), .din(RegisterFile_rs2_data), .data(ram_1_data), .str(Control_Unit_store_en),
    .sel(1'b1), .clk(clk_out), .ld(Control_Unit_load_en), .clr(reset));

  // Notes on the sheet:
  //   contents of rom_1 (hex, n*v repeats v):
  //   100293 313 532223 432383 2200093 2d00113 2d00113 3600193 ff1ff0ef
  //   SINGLE CYCLE RV32-I PROCESSOR
endmodule

module Diverter (
  input  [31:0] in,
  input  en,
  output [31:0] ALU_out,
  output [23:0] Load_out
);

  wire [31:24] demultiplexer_1_out1;

  Demultiplexer #(.width(32), .enable("false")) demultiplexer_1 (
    .out0(ALU_out), .out1({demultiplexer_1_out1, Load_out}), .in(in), .sel(en));
endmodule

module PC_Next (
  input  [31:0] imm,
  input  [31:0] PC_in,
  input  [31:0] rs1_in,
  input  jalr_en,
  output [31:0] nPC_out
);

  wire [31:0] multiplexer_1_out;

  Multiplexer #(.width(32), .enable("false")) multiplexer_1 (
    .in0(PC_in), .in1(rs1_in), .out(multiplexer_1_out), .sel(jalr_en));
  Adder #(.width(32)) adder_1 (.a(imm), .b(multiplexer_1_out), .out(nPC_out));  // open: cin, cout
endmodule

module Write_Type (
  input  [31:0] ALU_in,
  input  Branch_en,
  input  Load_en,
  input  nPC_en,
  input  auipc_en,
  input  lui_en,
  input  [31:0] Load_in,
  input  [31:0] nPC_in,
  input  [31:0] auipc_in,
  input  [31:0] lui_in,
  output [31:0] out,
  output Branch_out
);

  wire [31:0] adder_1_out, demultiplexer_1_out0, multiplexer_1_out, multiplexer_2_out, multiplexer_3_out;
  wire [31:1] demultiplexer_1_out1;

  Demultiplexer #(.width(32), .enable("false")) demultiplexer_1 (
    .out0(demultiplexer_1_out0), .out1({demultiplexer_1_out1, Branch_out}), .in(ALU_in), .sel(Branch_en));
  Adder #(.width(32)) adder_1 (.a(32'h4), .b(nPC_in), .out(adder_1_out));  // open: cin, cout
  Multiplexer #(.width(32), .enable("false")) multiplexer_1 (
    .in0(demultiplexer_1_out0), .in1(Load_in), .out(multiplexer_1_out), .sel(Load_en));
  Multiplexer #(.width(32), .enable("false")) multiplexer_2 (
    .in0(multiplexer_1_out), .in1(adder_1_out), .out(multiplexer_2_out), .sel(nPC_en));
  Multiplexer #(.width(32), .enable("false")) multiplexer_3 (
    .in0(multiplexer_2_out), .in1(auipc_in), .out(multiplexer_3_out), .sel(auipc_en));
  Multiplexer #(.width(32), .enable("false")) multiplexer_4 (
    .in0(multiplexer_3_out), .in1(lui_in), .out(out), .sel(lui_en));
endmodule

module U_Inst (
  input  [31:0] imm,
  input  [31:0] PC_in,
  output [31:0] lui_out,
  output [31:0] auipc_out
);

  Shifter #(.width(32)) shifter_1 (.in(imm), .\dist (5'b01100), .out(lui_out));
  Adder #(.width(32)) adder_1 (.a(lui_out), .b(PC_in), .out(auipc_out));  // open: cin, cout
endmodule

module Test (
  input  clk,
  input  reset,
  output [31:0] out_3,
  output [31:0] out_4,
  output [31:0] out_5,
  output [31:0] rs1_data,
  output [31:0] out_7,
  output [31:0] ALU_out,
  output [31:0] nPC,
  output [4:0] out_10,
  output [6:0] opcode,
  output [4:0] rd,
  output [31:0] inst_out_from_Fetch,
  output [31:0] rs2_data,
  output [4:0] rs1,
  output [31:0] PC_out,
  output [4:0] rs2,
  output [31:0] imm,
  output [2:0] func3,
  output [6:0] func7
);

  wire comparator_1_eq, comparator_2_eq, comparator_3_eq, comparator_4_eq, comparator_5_eq, comparator_6_eq,
       comparator_7_eq, comparator_8_eq, comparator_9_eq, comparator_9_gt, comparator_9_lt, comparator_10_eq,
       comparator_10_gt, comparator_10_lt, decoder_1_out0, decoder_1_out3, decoder_1_out4, decoder_1_out5,
       decoder_1_out6, decoder_1_out8, decoder_1_out12, decoder_1_out13, decoder_1_out14, decoder_1_out24,
       decoder_1_out25, decoder_1_out27, decoder_1_out28, decoder_2_out1, decoder_3_out1, decoder_3_out2,
       decoder_3_out3, decoder_3_out4, decoder_3_out5, decoder_3_out6, decoder_3_out7, decoder_3_out8,
       decoder_3_out9, decoder_3_out10, decoder_3_out11, decoder_3_out12, decoder_3_out13, decoder_3_out14,
       decoder_3_out15, decoder_3_out16, decoder_3_out17, decoder_3_out18, decoder_3_out19, decoder_3_out20,
       decoder_3_out21, decoder_3_out22, decoder_3_out23, decoder_3_out24, decoder_3_out25, decoder_3_out26,
       decoder_3_out27, decoder_3_out28, decoder_3_out29, decoder_3_out30, decoder_3_out31, not_1_out,
       not_2_out, not_3_out, not_4_out, not_5_out, not_6_out, not_7_out, or_1_out, or_2_out, or_3_out,
       or_4_out, or_10_out, or_11_out, or_12_out, or_14_out, or_15_out;
  wire [4:0] bit_extender_6_out;
  wire [17:0] bitselector_4_out;
  wire [24:0] bitselector_1_out, bitselector_2_out, bitselector_3_out, bitselector_5_out, bitselector_6_out;
  wire [31:0] adder_2_out, adder_3_out, adder_5_out, and_1_out, bit_extender_1_out, bit_extender_2_out,
       bit_extender_3_out, bit_extender_4_out, bit_extender_5_out, bit_extender_7_out, bit_extender_8_out,
       bit_extender_9_out, bit_extender_10_out, bit_extender_11_out, bit_extender_12_out,
       demultiplexer_1_out0, demultiplexer_1_out1, demultiplexer_2_out0, demultiplexer_2_out1,
       multiplexer_1_out, multiplexer_2_out, multiplexer_3_out, multiplexer_4_out, multiplexer_6_out,
       multiplexer_9_out, or_13_out, ram_1_data, shifter_2_out, shifter_3_out, shifter_4_out,
       subtractor_1_out, x0_q, x1_q, x2_q, x3_q, x4_q, x5_q, x6_q, x7_q, x8_q, x9_q, x10_q, x11_q, x12_q,
       x13_q, x14_q, x15_q, x16_q, x17_q, x18_q, x19_q, x20_q, x21_q, x22_q, x23_q, x24_q, x25_q, x26_q,
       x27_q, x28_q, x29_q, x30_q, x31_q, xor_1_out;

  Multiplexer #(.width(32), .enable("false")) multiplexer_1 (
    .in0(PC_out), .in1(rs1_data), .out(multiplexer_1_out), .sel(comparator_2_eq));
  Adder #(.width(32)) adder_1 (.a(imm), .b(multiplexer_1_out), .out(nPC));  // open: cin, cout
  Multiplexer #(.width(32), .enable("false")) multiplexer_2 (
    .in0(adder_2_out), .in1(nPC), .out(multiplexer_2_out), .sel(or_1_out));
  or or_1 (or_1_out, demultiplexer_1_out1[0], or_10_out);
  Register #(.width(32)) PC (.D(multiplexer_2_out), .en(1'b1), .Q(PC_out), .clk(clk), .clr(reset));
  Adder #(.width(32)) adder_2 (.a(32'h4), .b(PC_out), .out(adder_2_out));  // open: cin, cout
  ROM #(.addrWidth(24), .dataWidth(32)) rom_1 (.addr(PC_out[25:2]), .data(inst_out_from_Fetch));  // open: sel
  Decoder #(.select(5), .enable("false")) decoder_1 (
    .out0(decoder_1_out0), .out3(decoder_1_out3), .out4(decoder_1_out4), .out5(decoder_1_out5),
    .out6(decoder_1_out6), .out8(decoder_1_out8), .out12(decoder_1_out12), .out13(decoder_1_out13),
    .out14(decoder_1_out14), .out24(decoder_1_out24), .out25(decoder_1_out25), .out27(decoder_1_out27),
    .out28(decoder_1_out28), .sel(inst_out_from_Fetch[6:2]));  // open: out1, out2, out7, out9, out10, out11, out15, out16, out17, out18, out19, out20, out21, out22, out23, out26, out29, out30, out31
  or or_2 (or_2_out, decoder_1_out0, decoder_1_out3, decoder_1_out4, decoder_1_out6, decoder_1_out25, decoder_1_out28);
  or or_3 (or_3_out, decoder_1_out5, decoder_1_out13);
  or or_4 (or_4_out, decoder_1_out14, decoder_1_out12);
  BitSelector #(.width(25), .group(25)) bitselector_1 (
    .in(inst_out_from_Fetch[31:7]), .out(bitselector_1_out), .sel(not_1_out));
  not not_1 (not_1_out, or_2_out);
  not not_2 (not_2_out, decoder_1_out8);
  not not_3 (not_3_out, or_3_out);
  not not_4 (not_4_out, or_4_out);
  not not_5 (not_5_out, decoder_1_out24);
  not not_6 (not_6_out, decoder_1_out27);
  BitSelector #(.width(25), .group(25)) bitselector_2 (
    .in(inst_out_from_Fetch[31:7]), .out(bitselector_2_out), .sel(not_2_out));
  BitSelector #(.width(25), .group(25)) bitselector_3 (
    .in(inst_out_from_Fetch[31:7]), .out(bitselector_3_out), .sel(not_3_out));
  BitSelector #(.width(25), .group(25)) bitselector_4 (
    .in(inst_out_from_Fetch[31:7]), .out({func7, bitselector_4_out}), .sel(not_4_out));
  BitSelector #(.width(25), .group(25)) bitselector_5 (
    .in(inst_out_from_Fetch[31:7]), .out(bitselector_5_out), .sel(not_5_out));
  BitSelector #(.width(25), .group(25)) bitselector_6 (
    .in(inst_out_from_Fetch[31:7]), .out(bitselector_6_out), .sel(not_6_out));
  assign bit_extender_1_out = {{20{bitselector_1_out[24]}}, bitselector_1_out[24:13]};  // Bit_Extender bit_extender_1
  assign bit_extender_2_out = {{12{bitselector_3_out[24]}}, bitselector_3_out[24:5]};  // Bit_Extender bit_extender_2
  assign bit_extender_3_out = {{20{bitselector_2_out[24]}}, {bitselector_2_out[24:18], bitselector_2_out[4:0]}};  // Bit_Extender bit_extender_3
  assign bit_extender_4_out = {{19{bitselector_5_out[24]}}, {bitselector_5_out[24], bitselector_5_out[0], bitselector_5_out[23:18], bitselector_5_out[4:1], 1'b0}};  // Bit_Extender bit_extender_4
  Decoder #(.enable("false")) decoder_2 (.out1(decoder_2_out1), .sel(decoder_1_out27));  // open: out0
  assign bit_extender_5_out = {{11{bitselector_6_out[24]}}, {bitselector_6_out[24], bitselector_6_out[12:5], bitselector_6_out[13], bitselector_6_out[23:14], 1'b0}};  // Bit_Extender bit_extender_5
  assign bit_extender_6_out = {{4{1'b0}}, decoder_2_out1};  // Bit_Extender bit_extender_6
  Adder #(.width(32)) adder_3 (.a(32'h4), .b(PC_out), .out(adder_3_out));  // open: cin, cout
  assign rd = bitselector_1_out[4:0] | bitselector_3_out[4:0] | bitselector_4_out[4:0] | bit_extender_6_out;  // OR_Gate or_5, 5 bits wide
  assign func3 = bitselector_1_out[7:5] | bitselector_2_out[7:5] | bitselector_4_out[7:5] | bitselector_5_out[7:5];  // OR_Gate or_6, 3 bits wide
  assign rs1 = bitselector_1_out[12:8] | bitselector_2_out[12:8] | bitselector_4_out[12:8] | bitselector_5_out[12:8];  // OR_Gate or_7, 5 bits wide
  assign rs2 = bitselector_2_out[17:13] | bitselector_4_out[17:13] | bitselector_5_out[17:13];  // OR_Gate or_8, 5 bits wide
  assign imm = bit_extender_1_out | bit_extender_3_out | bit_extender_2_out | bit_extender_4_out | bit_extender_5_out;  // OR_Gate or_9, 32 bits wide
  Shifter #(.width(32)) shifter_1 (.in(imm), .\dist (5'b01100), .out(out_5));
  Adder #(.width(32)) adder_4 (.a(adder_2_out), .b(out_5), .out(out_3));  // open: cin, cout
  Demultiplexer #(.width(32), .enable("false")) demultiplexer_1 (
    .out0(demultiplexer_1_out0), .out1(demultiplexer_1_out1), .in(demultiplexer_2_out0), .sel(comparator_3_eq));
  Multiplexer #(.width(32), .enable("false")) multiplexer_3 (
    .in0(demultiplexer_1_out0), .in1(ram_1_data), .out(multiplexer_3_out), .sel(comparator_6_eq));
  Multiplexer #(.width(32), .enable("false")) multiplexer_4 (
    .in0(multiplexer_3_out), .in1(adder_3_out), .out(multiplexer_4_out), .sel(or_10_out));
  Multiplexer #(.width(32), .enable("false")) multiplexer_5 (
    .in0(multiplexer_4_out), .in1(out_3), .out(out_4), .sel(comparator_1_eq));
  Multiplexer #(.width(32), .enable("false")) multiplexer_6 (
    .in0(out_4), .in1(out_5), .out(multiplexer_6_out), .sel(comparator_8_eq));
  Decoder #(.select(5), .enable("false")) decoder_3 (
    .out1(decoder_3_out1), .out2(decoder_3_out2), .out3(decoder_3_out3), .out4(decoder_3_out4),
    .out5(decoder_3_out5), .out6(decoder_3_out6), .out7(decoder_3_out7), .out8(decoder_3_out8),
    .out9(decoder_3_out9), .out10(decoder_3_out10), .out11(decoder_3_out11), .out12(decoder_3_out12),
    .out13(decoder_3_out13), .out14(decoder_3_out14), .out15(decoder_3_out15), .out16(decoder_3_out16),
    .out17(decoder_3_out17), .out18(decoder_3_out18), .out19(decoder_3_out19), .out20(decoder_3_out20),
    .out21(decoder_3_out21), .out22(decoder_3_out22), .out23(decoder_3_out23), .out24(decoder_3_out24),
    .out25(decoder_3_out25), .out26(decoder_3_out26), .out27(decoder_3_out27), .out28(decoder_3_out28),
    .out29(decoder_3_out29), .out30(decoder_3_out30), .out31(decoder_3_out31), .sel(rd));  // open: out0
  or or_10 (or_10_out, comparator_2_eq, comparator_7_eq);
  Register #(.width(32)) x0 (.D({32{1'b0}}), .Q(x0_q));  // open: en, clk, clr
  Register #(.width(32)) x2 (.D(multiplexer_6_out), .en(decoder_3_out2), .Q(x2_q), .clk(clk), .clr(reset));
  Register #(.width(32)) x4 (.D(multiplexer_6_out), .en(decoder_3_out4), .Q(x4_q), .clk(clk), .clr(reset));
  Register #(.width(32)) x6 (.D(multiplexer_6_out), .en(decoder_3_out6), .Q(x6_q), .clk(clk), .clr(reset));
  Register #(.width(32)) x8 (.D(multiplexer_6_out), .en(decoder_3_out8), .Q(x8_q), .clk(clk), .clr(reset));
  Register #(.width(32)) x10 (.D(multiplexer_6_out), .en(decoder_3_out10), .Q(x10_q), .clk(clk), .clr(reset));
  Register #(.width(32)) x12 (.D(multiplexer_6_out), .en(decoder_3_out12), .Q(x12_q), .clk(clk), .clr(reset));
  Register #(.width(32)) x14 (.D(multiplexer_6_out), .en(decoder_3_out14), .Q(x14_q), .clk(clk), .clr(reset));
  Register #(.width(32)) x16 (.D(multiplexer_6_out), .en(decoder_3_out16), .Q(x16_q), .clk(clk), .clr(reset));
  Register #(.width(32)) x18 (.D(multiplexer_6_out), .en(decoder_3_out18), .Q(x18_q), .clk(clk), .clr(reset));
  Register #(.width(32)) x20 (.D(multiplexer_6_out), .en(decoder_3_out20), .Q(x20_q), .clk(clk), .clr(reset));
  Register #(.width(32)) x22 (.D(multiplexer_6_out), .en(decoder_3_out22), .Q(x22_q), .clk(clk), .clr(reset));
  Register #(.width(32)) x24 (.D(multiplexer_6_out), .en(decoder_3_out24), .Q(x24_q), .clk(clk), .clr(reset));
  Register #(.width(32)) x26 (.D(multiplexer_6_out), .en(decoder_3_out26), .Q(x26_q), .clk(clk), .clr(reset));
  Register #(.width(32)) x28 (.D(multiplexer_6_out), .en(decoder_3_out28), .Q(x28_q), .clk(clk), .clr(reset));
  Register #(.width(32)) x30 (.D(multiplexer_6_out), .en(decoder_3_out30), .Q(x30_q), .clk(clk), .clr(reset));
  Register #(.width(32)) x1 (.D(multiplexer_6_out), .en(decoder_3_out1), .Q(x1_q), .clk(clk), .clr(reset));
  Register #(.width(32)) x3 (.D(multiplexer_6_out), .en(decoder_3_out3), .Q(x3_q), .clk(clk), .clr(reset));
  Register #(.width(32)) x5 (.D(multiplexer_6_out), .en(decoder_3_out5), .Q(x5_q), .clk(clk), .clr(reset));
  Register #(.width(32)) x7 (.D(multiplexer_6_out), .en(decoder_3_out7), .Q(x7_q), .clk(clk), .clr(reset));
  Register #(.width(32)) x9 (.D(multiplexer_6_out), .en(decoder_3_out9), .Q(x9_q), .clk(clk), .clr(reset));
  Register #(.width(32)) x11 (.D(multiplexer_6_out), .en(decoder_3_out11), .Q(x11_q), .clk(clk), .clr(reset));
  Register #(.width(32)) x13 (.D(multiplexer_6_out), .en(decoder_3_out13), .Q(x13_q), .clk(clk), .clr(reset));
  Register #(.width(32)) x15 (.D(multiplexer_6_out), .en(decoder_3_out15), .Q(x15_q), .clk(clk), .clr(reset));
  Register #(.width(32)) x17 (.D(multiplexer_6_out), .en(decoder_3_out17), .Q(x17_q), .clk(clk), .clr(reset));
  Register #(.width(32)) x19 (.D(multiplexer_6_out), .en(decoder_3_out19), .Q(x19_q), .clk(clk), .clr(reset));
  Register #(.width(32)) x21 (.D(multiplexer_6_out), .en(decoder_3_out21), .Q(x21_q), .clk(clk), .clr(reset));
  Register #(.width(32)) x23 (.D(multiplexer_6_out), .en(decoder_3_out23), .Q(x23_q), .clk(clk), .clr(reset));
  Register #(.width(32)) x25 (.D(multiplexer_6_out), .en(decoder_3_out25), .Q(x25_q), .clk(clk), .clr(reset));
  Register #(.width(32)) x27 (.D(multiplexer_6_out), .en(decoder_3_out27), .Q(x27_q), .clk(clk), .clr(reset));
  Register #(.width(32)) x29 (.D(multiplexer_6_out), .en(decoder_3_out29), .Q(x29_q), .clk(clk), .clr(reset));
  Register #(.width(32)) x31 (.D(multiplexer_6_out), .en(decoder_3_out31), .Q(x31_q), .clk(clk), .clr(reset));
  Multiplexer #(.select(5), .width(32), .enable("false")) multiplexer_7 (
    .in0(x0_q), .in1(x1_q), .in2(x2_q), .in3(x3_q), .in4(x4_q), .in5(x5_q), .in6(x6_q), .in7(x7_q),
    .in8(x8_q), .in9(x9_q), .in10(x10_q), .in11(x11_q), .in12(x12_q), .in13(x13_q), .in14(x14_q),
    .in15(x15_q), .in16(x16_q), .in17(x17_q), .in18(x18_q), .in19(x19_q), .in20(x20_q), .in21(x21_q),
    .in22(x22_q), .in23(x23_q), .in24(x24_q), .in25(x25_q), .in26(x26_q), .in27(x27_q), .in28(x28_q),
    .in29(x29_q), .in30(x30_q), .in31(x31_q), .out(rs1_data), .sel(rs1));
  Multiplexer #(.select(5), .width(32), .enable("false")) multiplexer_8 (
    .in0(x0_q), .in1(x1_q), .in2(x2_q), .in3(x3_q), .in4(x4_q), .in5(x5_q), .in6(x6_q), .in7(x7_q),
    .in8(x8_q), .in9(x9_q), .in10(x10_q), .in11(x11_q), .in12(x12_q), .in13(x13_q), .in14(x14_q),
    .in15(x15_q), .in16(x16_q), .in17(x17_q), .in18(x18_q), .in19(x19_q), .in20(x20_q), .in21(x21_q),
    .in22(x22_q), .in23(x23_q), .in24(x24_q), .in25(x25_q), .in26(x26_q), .in27(x27_q), .in28(x28_q),
    .in29(x29_q), .in30(x30_q), .in31(x31_q), .out(rs2_data), .sel(rs2));
  Comparator #(.width(5), .mode("unsigned")) comparator_1 (
    .a(5'b00101), .b(inst_out_from_Fetch[6:2]), .eq(comparator_1_eq));  // open: gt, lt
  Comparator #(.width(5)) comparator_2 (
    .a(5'b11001), .b(inst_out_from_Fetch[6:2]), .eq(comparator_2_eq));  // open: gt, lt
  Comparator #(.width(5), .mode("unsigned")) comparator_3 (
    .a(5'b11000), .b(inst_out_from_Fetch[6:2]), .eq(comparator_3_eq));  // open: gt, lt
  Comparator #(.width(5), .mode("unsigned")) comparator_4 (
    .a(5'b00100), .b(inst_out_from_Fetch[6:2]), .eq(comparator_4_eq));  // open: gt, lt
  Comparator #(.width(5), .mode("unsigned")) comparator_5 (
    .a(5'b01000), .b(inst_out_from_Fetch[6:2]), .eq(comparator_5_eq));  // open: gt, lt
  Comparator #(.width(5), .mode("unsigned")) comparator_6 (
    .a({5{1'b0}}), .b(inst_out_from_Fetch[6:2]), .eq(comparator_6_eq));  // open: gt, lt
  Comparator #(.width(5), .mode("unsigned")) comparator_7 (
    .a(inst_out_from_Fetch[6:2]), .b(5'b11011), .eq(comparator_7_eq));  // open: gt, lt
  Comparator #(.width(5), .mode("unsigned")) comparator_8 (
    .a(5'b01101), .b(inst_out_from_Fetch[6:2]), .eq(comparator_8_eq));  // open: gt, lt
  or or_11 (or_11_out, comparator_4_eq, comparator_5_eq, comparator_6_eq);
  or or_12 (or_12_out, comparator_5_eq, comparator_6_eq);
  Multiplexer #(.width(32), .enable("false")) multiplexer_9 (
    .in0(rs2_data), .in1(imm), .out(multiplexer_9_out), .sel(or_11_out));
  Comparator #(.width(32)) comparator_9 (
    .a(rs1_data), .b(multiplexer_9_out), .gt(comparator_9_gt), .eq(comparator_9_eq), .lt(comparator_9_lt));
  Comparator #(.width(32), .mode("unsigned")) comparator_10 (
    .a(rs1_data), .b(multiplexer_9_out), .gt(comparator_10_gt), .eq(comparator_10_eq), .lt(comparator_10_lt));
  Adder #(.width(32)) adder_5 (.a(rs1_data), .b(multiplexer_9_out), .out(adder_5_out));  // open: cin, cout
  Subtractor #(.width(32)) subtractor_1 (
    .a(rs1_data), .b(multiplexer_9_out), .out(subtractor_1_out));  // open: bin, bout
  Shifter #(.width(32)) shifter_2 (.in(rs1_data), .\dist (multiplexer_9_out[4:0]), .out(shifter_2_out));
  assign xor_1_out = rs1_data ^ multiplexer_9_out;  // XOR_Gate xor_1, 32 bits wide
  Shifter #(.width(32), .shift("lr")) shifter_3 (.in(rs1_data), .\dist (multiplexer_9_out[4:0]), .out(shifter_3_out));
  Shifter #(.width(32), .shift("ar")) shifter_4 (.in(rs1_data), .\dist (multiplexer_9_out[4:0]), .out(shifter_4_out));
  assign or_13_out = rs1_data | multiplexer_9_out;  // OR_Gate or_13, 32 bits wide
  assign and_1_out = rs1_data & multiplexer_9_out;  // AND_Gate and_1, 32 bits wide
  assign bit_extender_7_out = {{31{1'b0}}, comparator_9_eq};  // Bit_Extender bit_extender_7
  assign bit_extender_8_out = {{31{1'b0}}, not_7_out};  // Bit_Extender bit_extender_8
  not not_7 (not_7_out, comparator_9_eq);
  assign bit_extender_9_out = {{31{1'b0}}, comparator_9_lt};  // Bit_Extender bit_extender_9
  or or_14 (or_14_out, comparator_9_gt, comparator_9_eq);
  assign bit_extender_10_out = {{31{1'b0}}, or_14_out};  // Bit_Extender bit_extender_10
  assign bit_extender_11_out = {{31{1'b0}}, comparator_10_lt};  // Bit_Extender bit_extender_11
  or or_15 (or_15_out, comparator_10_gt, comparator_10_eq);
  assign bit_extender_12_out = {{31{1'b0}}, or_15_out};  // Bit_Extender bit_extender_12
  Multiplexer #(.select(5), .width(32), .enable("false")) multiplexer_10 (
    .in0(bit_extender_7_out), .in1(bit_extender_8_out), .in2(adder_5_out), .in4(bit_extender_9_out),
    .in5(bit_extender_10_out), .in6(bit_extender_11_out), .in7(bit_extender_12_out), .in16(adder_5_out),
    .in17(shifter_2_out), .in18(bit_extender_9_out), .in19(bit_extender_11_out), .in20(xor_1_out),
    .in21(shifter_3_out), .in22(or_13_out), .in23(and_1_out), .in24(subtractor_1_out), .in29(shifter_4_out),
    .out(ALU_out), .sel({inst_out_from_Fetch[4], func7[5], func3}));  // open: in3, in8, in9, in10, in11, in12, in13, in14, in15, in25, in26, in27, in28, in30, in31
  Demultiplexer #(.width(32), .enable("false")) demultiplexer_2 (
    .out0(demultiplexer_2_out0), .out1(demultiplexer_2_out1), .in(ALU_out), .sel(or_12_out));
  RAM #(.addrWidth(24), .dataWidth(32), .bus("separate")) ram_1 (
    .addr(demultiplexer_2_out1[23:0]), .din(rs2_data), .data(ram_1_data), .str(or_12_out), .sel(1'b1),
    .clk(clk), .ld(comparator_6_eq), .clr(reset));

  assign opcode = inst_out_from_Fetch[6:0];
  assign out_7 = imm;
  assign out_10 = {inst_out_from_Fetch[4], func7[5], func3};

  // Notes on the sheet:
  //   contents of rom_1 (hex, n*v repeats v):
  //   200293 300313 6283b3
endmodule
