// Logisim project Control Unit.circ as structural Verilog: 1 circuit, main circuit Control Unit
module Control_Unit (
  input  [4:0] ID,
  output Diverter_en,
  output jalr_en,
  output op2Sel,
  output store_en,
  output load_en,
  output jal_en,
  output lui_en,
  output branch_en,
  output auipc_en
);

  wire comparator_2_eq;

  Comparator #(.width(5), .mode("unsigned")) comparator_1 (.a(ID), .b(5'b11001), .eq(jalr_en));  // open: gt, lt
  Comparator #(.width(5), .mode("unsigned")) comparator_2 (.a(ID), .b(5'b00100), .eq(comparator_2_eq));  // open: gt, lt
  Comparator #(.width(5), .mode("unsigned")) comparator_3 (.a(ID), .b(5'b01000), .eq(store_en));  // open: gt, lt
  Comparator #(.width(5), .mode("unsigned")) comparator_4 (.a(ID), .b({5{1'b0}}), .eq(load_en));  // open: gt, lt
  Comparator #(.width(5), .mode("unsigned")) comparator_5 (.a(ID), .b(5'b11011), .eq(jal_en));  // open: gt, lt
  Comparator #(.width(5), .mode("unsigned")) comparator_6 (.a(ID), .b(5'b01101), .eq(lui_en));  // open: gt, lt
  Comparator #(.width(5), .mode("unsigned")) comparator_7 (.a(ID), .b(5'b11000), .eq(branch_en));  // open: gt, lt
  Comparator #(.width(5), .mode("unsigned")) comparator_8 (.a(ID), .b(5'b00101), .eq(auipc_en));  // open: gt, lt
  or or_1 (Diverter_en, store_en, load_en);
  or or_2 (op2Sel, comparator_2_eq, store_en, load_en);
endmodule
